# Fritzing sketch Untitled Sketch 2 (saved by Fritzing 0.9.3b)
breadboards: 1

parts:
  Part1 = Arduino Ethernet Shield (Rev3)
  BeagleBone1 = BeagleBone Black
  U1 = TMP36 [package=to-92-kit]
  R1 = Resistor [tolerance=±5% resistance=220 package=THT]

nets:
  GND: Part1.GND, BeagleBone1.no_name_yet#1, U1.GND
  N1: Part1.A5/SCL, U1.VOUT, R1.Pin_0
  N2: Part1.TX/D1, BeagleBone1.no_name_yet#26
  5V: Part1.5V, U1.VCC, R1.Pin_1

custom parts:
  BeagleBone Black: BeagleBone Black rev. A5B
